// Logisim project 32bitFPGA_2.circ as structural Verilog: 11 circuits, main circuit CPUtest
module main (
  input  [31:0] in_1
);

  wire Cl, CPU_1_inp, CPU_1_outp, CPU_1_ram_in, CPU_1_ram_out, n7_segment_display_1_p1,
       n7_segment_display_2_p1, n7_segment_display_3_p1, n7_segment_display_4_p1, rgb_video_1_p1,
       rgb_video_1_p2, rgb_video_1_p3;
  wire [1:0] io_1_io1, io_1_io2, io_1_io3, io_1_io4;
  wire [2:0] CPU_1_deviceid;
  wire [6:0] bit_extender_3_out, keyboard_1_data, rgb_video_1_p4, rgb_video_1_p5;
  wire [12:0] binary_to_bcd_converter_1_p1;
  wire [23:0] rgb_video_1_p6;
  wire [31:0] bit_extender_1_out, BRAM_1_d_out, CPU_1_outp_data, CPU_1_ram_address, CPU_1_ram_datai,
       io_1_data_in, io_1_o2, io_1_o3, io_1_o4, register_1_q;

  Clock clock_1 (.out(Cl));
  Keyboard #(.trigger("falling")) keyboard_1 (.clk(Cl), .re(io_1_io1[1]), .data(keyboard_1_data));  // open: clr, avail
  Register #(.width(32)) register_1 (.D(io_1_o2), .en(io_1_io2[0]), .clk(Cl), .Q(register_1_q));  // open: clr
  // _7_Segment_Display 7_segment_display_1: pin names not known; wires that end beside it: n7_segment_display_1_p1, n7_segment_display_1_p1
  // BCD_to_7_Segment_decoder bcd_to_7_segment_decoder_1: pin names not known
  // Binary_to_BCD_converter #(.binvalue(13)) binary_to_bcd_converter_1: pin names not known; wires that end beside it: binary_to_bcd_converter_1_p1
  // _7_Segment_Display 7_segment_display_2: pin names not known; wires that end beside it: n7_segment_display_2_p1, n7_segment_display_2_p1
  // BCD_to_7_Segment_decoder bcd_to_7_segment_decoder_2: pin names not known
  // Probe on BRAM_1_d_out
  assign bit_extender_1_out = {{25{1'b0}}, keyboard_1_data};  // Bit_Extender bit_extender_1
  Bit_Extender #(.in_width(32), .out_width(13), .\type ("zero")) bit_extender_2 (
    .in(register_1_q), .out(binary_to_bcd_converter_1_p1));
  // _7_Segment_Display 7_segment_display_3: pin names not known; wires that end beside it: n7_segment_display_3_p1, n7_segment_display_3_p1
  // BCD_to_7_Segment_decoder bcd_to_7_segment_decoder_3: pin names not known
  // _7_Segment_Display 7_segment_display_4: pin names not known; wires that end beside it: n7_segment_display_4_p1, n7_segment_display_4_p1
  // BCD_to_7_Segment_decoder bcd_to_7_segment_decoder_4: pin names not known
  CPU CPU_1 (
    .INSTRUCTION(BRAM_1_d_out), .Cl(Cl), .Input_data(io_1_data_in), .RAM_address(CPU_1_ram_address),
    .RAM_IN(CPU_1_ram_in), .RAM_OUT(CPU_1_ram_out), .OUTP_DATA(CPU_1_outp_data), .DeviceID(CPU_1_deviceid),
    .INP(CPU_1_inp), .OUTP(CPU_1_outp), .RAM_DATAI(CPU_1_ram_datai));
  Bit_Extender #(.in_width(32), .out_width(7), .\type ("zero")) bit_extender_3 (.in(io_1_o4), .out(bit_extender_3_out));
  TTY tty_1 (.data(bit_extender_3_out), .clk(Cl), .we(io_1_io4[0]));  // open: clr
  IO io_1 (
    .deviceID(CPU_1_deviceid), .DATA_OUT(CPU_1_outp_data), .OUTP(CPU_1_outp), .iNP(CPU_1_inp),
    .i1(bit_extender_1_out), .i2(in_1), .o2(io_1_o2), .o3(io_1_o3), .o4(io_1_o4), .DATA_IN(io_1_data_in),
    .io1(io_1_io1), .io2(io_1_io2), .io3(io_1_io3), .io4(io_1_io4));  // open: i3, i4, i5, i6, i7, i8, o1, o5, o6, o7, o8, io5, io6, io7, io8
  Pull_Resistor pull_resistor_1 (.node(io_1_io4[0]));
  BRAM BRAM_1 (
    .Address(CPU_1_ram_address), .clock(Cl), .write(CPU_1_ram_in), .Read(CPU_1_ram_out),
    .D_IN(CPU_1_ram_datai), .D_OUT(BRAM_1_d_out));
  // RGB_Video #(.cursor("No Cursor")) rgb_video_1: pin names not known; wires that end beside it: rgb_video_1_p1, rgb_video_1_p2, rgb_video_1_p3, rgb_video_1_p4, rgb_video_1_p5, rgb_video_1_p6
  DisplayBuffer displaybuffer_1 (
    .CL(Cl), .Inp(io_1_io3[0]), .DATA(io_1_o3), .RGB(rgb_video_1_p6), .X(rgb_video_1_p4), .Y(rgb_video_1_p5),
    .Enable(rgb_video_1_p3), .RESET(rgb_video_1_p1), .clout(rgb_video_1_p2));
endmodule

module CPU (
  input  [31:0] INSTRUCTION,
  input  Cl,
  input  [31:0] Input_data,
  output [31:0] RAM_address,
  output RAM_IN,
  output RAM_OUT,
  output [31:0] OUTP_DATA,
  output [2:0] DeviceID,
  output INP,
  output OUTP,
  output [31:0] RAM_DATAI
);

  wire ALU_1_set_flags, CU_1_mux_alu, CU_1_write;
  wire [1:0] CU_1_mux_reg;
  wire [2:0] ALU_1_flags;
  wire [4:0] CU_1_func, CU_1_rdst, CU_1_rsrc1, CU_1_rsrc2, CU_1_shifts;
  wire [31:0] ALU_1_c, CU_1_immediate, multiplexer_1_out, multiplexer_2_out, Registry_1_b_out;

  // Probe on INSTRUCTION
  CU CU_1 (
    .Instruction(INSTRUCTION), .FLAGS(ALU_1_flags), .set_FLAGS(ALU_1_set_flags), .Reg_InA(OUTP_DATA),
    .Clock(Cl), .REG_inB(Registry_1_b_out), .Shifts(CU_1_shifts), .write(CU_1_write),
    .Immediate(CU_1_immediate), .Inp(INP), .Rsrc1(CU_1_rsrc1), .Outp(OUTP), .MUX_ALU(CU_1_mux_alu),
    .Rsrc2(CU_1_rsrc2), .MUX_REG(CU_1_mux_reg), .Rdst(CU_1_rdst), .Func(CU_1_func), .RAM_OUT(RAM_OUT),
    .RAM_IN(RAM_IN), .RAM_address(RAM_address));
  Bit_Extender #(.in_width(32), .out_width(3)) bit_extender_1 (.in(CU_1_immediate), .out(DeviceID));
  Multiplexer #(.width(32)) multiplexer_1 (
    .in0(CU_1_immediate), .in1(Registry_1_b_out), .out(multiplexer_1_out), .sel(CU_1_mux_alu));
  Multiplexer #(.select(2), .width(32)) multiplexer_2 (
    .in0(OUTP_DATA), .in1(ALU_1_c), .in2(CU_1_immediate), .in3(Input_data), .out(multiplexer_2_out),
    .sel(CU_1_mux_reg));
  ALU ALU_1 (
    .sh(CU_1_shifts), .A(OUTP_DATA), .B(multiplexer_1_out), .func(CU_1_func), .C(ALU_1_c),
    .FLAGS(ALU_1_flags), .set_FLAGS(ALU_1_set_flags));
  Registry Registry_1 (
    .DATA_in(multiplexer_2_out), .CL(Cl), .A_address(CU_1_rsrc1), .B_address(CU_1_rsrc2),
    .write_address(CU_1_rdst), .write(CU_1_write), .A_OUT(OUTP_DATA), .B_OUT(Registry_1_b_out));

  assign RAM_DATAI = OUTP_DATA;

  // Notes on the sheet:
  //   0 Imm->B
  //   1 B_OUT->B
  //   0 B_OUT ->DATA_in 
  //   10 C -> DATA_in
  //   11 Imm -> DATA_in
endmodule

module BRAM (
  input  [31:0] Address,
  input  clock,
  input  write,
  input  Read,
  input  [31:0] D_IN,
  output [31:0] D_OUT
);

  wire not_1_out;
  wire [11:0] bit_extender_1_out, register_1_q;

  Register #(.width(12)) register_1 (.D(bit_extender_1_out), .clk(clock), .Q(register_1_q));  // open: en, clr
  Bit_Extender #(.in_width(32), .out_width(12)) bit_extender_1 (.in(Address), .out(bit_extender_1_out));
  RAM #(.addrWidth(12), .dataWidth(32), .\type ("nonvolatile")) RAM_1 (
    .addr(register_1_q), .we(write), .oe(Read), .clk(not_1_out), .din(D_IN), .dout(D_OUT));
  not not_1 (not_1_out, clock);
  Pull_Resistor pull_resistor_1 (.node(D_OUT));
endmodule

module CPUtest (
  input  in_1
);

  wire CU_1_p3, CU_1_p7, CU_1_p8, CU_1_p9, CU_1_p10, CU_1_p11, CU_1_p14, CU_1_p15;
  wire [1:0] CU_1_p12;
  wire [2:0] CU_1_p2;
  wire [4:0] CU_1_p5, CU_1_p13;
  wire [31:0] ALU_1_c, BRAM_1_d_out, CU_1_p6, CU_1_p16, multiplexer_1_out, multiplexer_2_out, Registry_1_p7,
       Registry_1_p8;

  BRAM BRAM_1 (
    .Address(CU_1_p16), .clock(in_1), .write(CU_1_p14), .Read(CU_1_p15), .D_IN(Registry_1_p7),
    .D_OUT(BRAM_1_d_out));
  // Probe on BRAM_1_d_out
  // CU CU_1: pin names not known; wires that end beside it: BRAM_1_d_out, CU_1_p2, CU_1_p3, in_1, CU_1_p5, CU_1_p6, CU_1_p7, CU_1_p8, CU_1_p9, CU_1_p10, CU_1_p11, CU_1_p12, CU_1_p13, CU_1_p14, CU_1_p15, CU_1_p16
  Multiplexer #(.width(32)) multiplexer_1 (.in0(CU_1_p6), .in1(Registry_1_p8), .out(multiplexer_1_out), .sel(CU_1_p11));
  Multiplexer #(.select(2), .width(32)) multiplexer_2 (
    .in0(Registry_1_p7), .in1(ALU_1_c), .in2(CU_1_p6), .out(multiplexer_2_out), .sel(CU_1_p12));  // open: in3
  ALU ALU_1 (
    .sh(CU_1_p5), .A(Registry_1_p7), .B(multiplexer_1_out), .func(CU_1_p13), .C(ALU_1_c), .FLAGS(CU_1_p2),
    .set_FLAGS(CU_1_p3));
  // Registry Registry_1: pin names not known; wires that end beside it: multiplexer_2_out, in_1, CU_1_p7, CU_1_p8, CU_1_p9, CU_1_p10, Registry_1_p7, Registry_1_p8

  // Notes on the sheet:
  //   1 B_OUT->B
  //   0 Imm->B
  //   0 B_OUT ->DATA_in 
  //   11 Imm -> DATA_in
  //   10 C -> DATA_in
endmodule

module CU (
  input  [31:0] Instruction,
  input  [2:0] FLAGS,
  input  set_FLAGS,
  input  [31:0] Reg_InA,
  input  Clock,
  input  [31:0] REG_inB,
  output [4:0] Shifts,
  output write,
  output [31:0] Immediate,
  output Inp,
  output [4:0] Rsrc1,
  output Outp,
  output MUX_ALU,
  output [4:0] Rsrc2,
  output [1:0] MUX_REG,
  output [4:0] Rdst,
  output [4:0] Func,
  output RAM_OUT,
  output RAM_IN,
  output [31:0] RAM_address
);

  wire and_1_out, and_2_out, and_3_out, and_4_out, and_5_out, and_6_out, Branch, ConditionsPassed,
       decoder_1_out0, decoder_1_out1, decoder_1_out2, decoder_1_out3, JMP, NoInc, not_1_out, not_2_out,
       not_3_out, not_4_out, or_3_out, or_4_out, or_6_out, read_out, register_1_q, register_3_q,
       register_5_q, toREG;
  wire [1:0] Conditions, ROM_1_data_2;
  wire [2:0] register_6_q;
  wire [4:0] Func_t, register_2_q, ROM_1_data_3;
  wire [5:0] Opcode;
  wire [6:0] ROM_1_data;
  wire [15:0] Immediate_t;
  wire [31:0] adder_1_out, adder_2_out, adder_3_out, bit_extender_1_out, bit_extender_2_out,
       bit_extender_3_out, bit_extender_4_out, multiplexer_2_out, multiplexer_4_out, multiplexer_8_out,
       multiplexer_9_out, PC, PC_COUNTER_q;

  and read (read_out, Opcode[0], Opcode[1], ~Opcode[2], ~Opcode[3], Opcode[4], ~Opcode[5]);  // AND_Gate
  or or_1 (NoInc, read_out, RAM_IN);
  and write_A (RAM_IN, ~Opcode[0], ~Opcode[1], Opcode[2], ~Opcode[3], Opcode[4], ~Opcode[5]);  // AND_Gate
  Register #(.width(1)) register_1 (.D(read_out), .clk(Clock), .Q(register_1_q));  // open: en, clr
  Register #(.width(5)) register_2 (.D(Rdst), .en(read_out), .clk(Clock), .Q(register_2_q));  // open: clr
  Register #(.width(1)) register_3 (.D(RAM_IN), .clk(Clock), .Q(register_3_q));  // open: en, clr
  not not_1 (not_1_out, RAM_IN);
  Register #(.trigger("falling"), .width(1)) register_4 (.D(register_1_q), .clk(Clock), .Q(toREG));  // open: en, clr
  Register #(.trigger("falling"), .width(1)) register_5 (
    .D(register_3_q), .clk(Clock), .Q(register_5_q));  // open: en, clr
  not not_2 (not_2_out, register_5_q);
  Multiplexer #(.width(32)) multiplexer_1 (
    .in0({32{1'b0}}), .in1(multiplexer_2_out),
    .out({Opcode, Rdst, Rsrc1, Immediate_t[15:11], Shifts, Func_t, Immediate_t[0]}), .sel(not_2_out));
  Multiplexer #(.width(32)) multiplexer_2 (
    .in0(Instruction), .in1({{6{1'b0}}, register_2_q, {21{1'b0}}}), .out(multiplexer_2_out), .sel(toREG));
  buf or_2 (RAM_OUT, not_1_out);  // OR_Gate
  ROM #(.addrWidth(6), .dataWidth(16)) ROM_1 (
    .addr(Opcode),
    .data({Conditions, Branch, JMP, ROM_1_data_3, ROM_1_data[6], ROM_1_data_2, MUX_ALU, Outp, Inp, ROM_1_data[0]}));
  and and_1 (and_1_out, Opcode[0], ~or_3_out);  // AND_Gate
  or or_3 (or_3_out, Opcode[1], Opcode[2], Opcode[3], Opcode[4], Opcode[5]);
  and and_2 (and_2_out, Immediate_t[0], and_1_out);
  or or_4 (or_4_out, set_FLAGS, and_2_out);
  Register #(.width(3)) register_6 (.D(FLAGS), .en(or_4_out), .clk(Clock), .Q(register_6_q));  // open: clr
  assign bit_extender_1_out = {{6{Rdst[4]}}, {Rdst, Rsrc1, Immediate_t[15:11], Shifts, Func_t, Immediate_t[0]}};  // Bit_Extender bit_extender_1
  or or_5 (write, toREG, ROM_1_data[0]);
  assign bit_extender_2_out = {{6{1'b0}}, {Rdst, Rsrc1, Immediate_t[15:11], Shifts, Func_t, Immediate_t[0]}};  // Bit_Extender bit_extender_2
  Adder #(.width(32)) adder_1 (.a(bit_extender_1_out), .b(PC), .out(adder_1_out));  // open: cin, cout
  Multiplexer #(.width(2)) multiplexer_3 (.in0(ROM_1_data_2), .in1(2'b10), .out(MUX_REG), .sel(toREG));
  Multiplexer #(.width(32)) multiplexer_4 (
    .in0(bit_extender_2_out), .in1(adder_1_out), .out(multiplexer_4_out), .sel(Branch));
  or or_6 (or_6_out, JMP, Branch);
  and and_3 (and_3_out, or_6_out, ConditionsPassed);
  Multiplexer #(.width(5)) multiplexer_5 (.in0(ROM_1_data_3), .in1(Func_t), .out(Func), .sel(ROM_1_data[6]));
  Decoder #(.select(2)) decoder_1 (
    .out0(decoder_1_out0), .out1(decoder_1_out1), .out2(decoder_1_out2), .out3(decoder_1_out3),
    .sel(Conditions));  // open: en
  Adder #(.width(32)) adder_2 (.a(multiplexer_4_out), .b(32'h1), .out(adder_2_out));  // open: cin, cout
  assign bit_extender_3_out = {{16{Immediate_t[15]}}, {Immediate_t[15:11], Shifts, Func_t, Immediate_t[0]}};  // Bit_Extender bit_extender_3
  and and_4 (and_4_out, register_6_q[0], decoder_1_out3);
  and and_5 (and_5_out, register_6_q[1], decoder_1_out2);
  and and_6 (and_6_out, register_6_q[2], decoder_1_out1);
  Counter #(.max('hffffffff), .width(32)) PC_COUNTER (
    .load(and_3_out), .up(not_3_out), .count(not_3_out), .clk(Clock), .D(adder_2_out), .Q(PC_COUNTER_q));  // open: clr, carry
  not not_3 (not_3_out, NoInc);
  Multiplexer #(.width(32)) multiplexer_6 (.in0(bit_extender_3_out), .in1(Instruction), .out(Immediate), .sel(toREG));
  Multiplexer #(.width(5)) multiplexer_7 (.in0(Immediate_t[15:11]), .in1(Rdst), .out(Rsrc2), .sel(RAM_IN));
  or or_7 (ConditionsPassed, and_4_out, and_5_out, and_6_out, decoder_1_out0);
  assign bit_extender_4_out = {{16{1'b0}}, {Immediate_t[15:11], Shifts, Func_t, Immediate_t[0]}};  // Bit_Extender bit_extender_4
  Multiplexer #(.width(32)) multiplexer_8 (.in0(Reg_InA), .in1(REG_inB), .out(multiplexer_8_out), .sel(RAM_IN));
  not not_4 (not_4_out, NoInc);
  Adder #(.width(32)) adder_3 (.a(bit_extender_4_out), .b(multiplexer_8_out), .out(adder_3_out));  // open: cin, cout
  Multiplexer #(.width(32)) multiplexer_9 (.in0(PC), .in1(multiplexer_4_out), .out(multiplexer_9_out), .sel(and_3_out));
  Multiplexer #(.width(32)) multiplexer_10 (
    .in0(adder_3_out), .in1(multiplexer_9_out), .out(RAM_address), .sel(not_4_out));
  Register #(.trigger("falling"), .width(32)) register_7 (.D(PC_COUNTER_q), .clk(Clock), .Q(PC));  // open: en, clr

  // Other names for the same wires on the sheet: Jmp_Immediate[25:0] = {Rdst, Rsrc1, Immediate_t[15:11], Shifts, Func_t, Immediate_t[0]};
  //   SrcReg1[4:0] = Rsrc1; DstReg[4:0] = Rdst; Cl = Clock; set_flags_t = Immediate_t[0];
  //   Immediate_t[10:1] = {Shifts, Func_t}; SrcReg2[4:0] = Immediate_t[15:11]; OverrideAddress = NoInc;
  //   OverrideReg = RAM_IN

  // Notes on the sheet:
  //   R-Type
  //   contents of ROM_1 (hex, n*v repeats v):
  //   0 59 11 0 111 0 211 291 1 391 710 790 21 4*0 33 4 0 0 1000 5000 9000 d000 2000 a000 6000 e000 7*0
  //   2000 a000 6000
  //   I-Type
  //   0 Imm->B
  //   1 B_OUT->B
  //   J-Type
  //   A>B
  //   0 B_OUT ->DATA_in 
  //   01 C -> DATA_in
  //   10 Imm -> DATA_in
  //   A<B
  //   1 use Funct to ALU
  //   0 use synthetic Funct
endmodule

module ALU (
  input  [4:0] sh,
  input  [31:0] A,
  input  [31:0] B,
  input  [4:0] func,
  output [31:0] C,
  output [2:0] FLAGS,
  output set_FLAGS
);

  wire [1:0] decoder_1_out14;
  wire [2:0] comparator_1_gt, comparator_2_gt, comparator_3_gt;
  wire [31:0] adder_1_out, and_1_out, not_1_out, or_2_out, shifter_1_out, shifter_2_out, shifter_3_out,
       shifter_4_out, shifter_5_out, subtractor_1_out, subtractor_2_out, xor_1_out;

  Decoder #(.select(5)) decoder_1 (
    .out14(decoder_1_out14[0]), .out15(decoder_1_out14[1]), .sel(func));  // open: out0, out1, out2, out3, out4, out5, out6, out7, out8, out9, out10, out11, out12, out13, out16, out17, out18, out19, out20, out21, out22, out23, out24, out25, out26, out27, out28, out29, out30, out31, en
  or or_1 (set_FLAGS, decoder_1_out14[1], decoder_1_out14[0]);
  Adder #(.width(32)) adder_1 (.a(A), .b(B), .out(adder_1_out));  // open: cin, cout
  Subtractor #(.width(32)) subtractor_1 (.a(A), .b(B), .out(subtractor_1_out));  // open: bin, bout
  assign and_1_out = B & A;  // AND_Gate and_1, 32 bits wide
  assign or_2_out = B | A;  // OR_Gate or_2, 32 bits wide
  assign not_1_out = ~A;  // NOT_Gate not_1, 32 bits wide
  assign xor_1_out = A ^ B;  // XOR_Gate xor_1, 32 bits wide
  Shifter #(.width(32)) shifter_1 (.in(A), .\dist (sh), .out(shifter_1_out));
  Shifter #(.shift("lr"), .width(32)) shifter_2 (.in(A), .\dist (sh), .out(shifter_2_out));
  Shifter #(.shift("ar"), .width(32)) shifter_3 (.in(A), .\dist (sh), .out(shifter_3_out));
  Shifter #(.shift("rl"), .width(32)) shifter_4 (.in(A), .\dist (sh), .out(shifter_4_out));
  Shifter #(.shift("rr"), .width(32)) shifter_5 (.in(A), .\dist (sh), .out(shifter_5_out));
  Comparator #(.width(32)) comparator_1 (
    .a(A), .b(B), .gt(comparator_1_gt[0]), .eq(comparator_1_gt[1]), .lt(comparator_1_gt[2]));
  Comparator #(.mode("unsigned"), .width(32)) comparator_2 (
    .a(A), .b(B), .gt(comparator_2_gt[0]), .eq(comparator_2_gt[1]), .lt(comparator_2_gt[2]));
  Multiplexer #(.select(2), .width(3)) multiplexer_1 (
    .in0(comparator_3_gt), .in1(comparator_1_gt), .in2(comparator_2_gt), .out(FLAGS), .sel(decoder_1_out14));  // open: in3
  Subtractor #(.width(32)) subtractor_2 (.a(A), .b(32'h1), .out(subtractor_2_out));  // open: bin, bout
  Multiplexer #(.select(5), .width(32)) multiplexer_2 (
    .in0(adder_1_out), .in2(subtractor_1_out), .in3(subtractor_2_out), .in4(and_1_out), .in5(or_2_out),
    .in6(not_1_out), .in7(xor_1_out), .in8(shifter_1_out), .in9(shifter_2_out), .in10(shifter_3_out),
    .in11(shifter_4_out), .in12(shifter_5_out), .in14(subtractor_1_out), .in15(subtractor_1_out), .out(C),
    .sel(func));  // open: in1, in13, in16, in17, in18, in19, in20, in21, in22, in23, in24, in25, in26, in27, in28, in29, in30, in31
  Comparator #(.width(32)) comparator_3 (
    .a(C), .b({32{1'b0}}), .gt(comparator_3_gt[0]), .eq(comparator_3_gt[1]), .lt(comparator_3_gt[2]));
endmodule

module Registry (
  input  [31:0] DATA_in,
  input  CL,
  input  [4:0] A_address,
  input  [4:0] B_address,
  input  [4:0] write_address,
  input  write,
  output [31:0] A_OUT,
  output [31:0] B_OUT
);

  wire decoder_1_out1, decoder_1_out2, decoder_1_out3, decoder_1_out4, decoder_1_out5, decoder_1_out6,
       decoder_1_out7, decoder_1_out8, decoder_1_out9, decoder_1_out10, decoder_1_out11, decoder_1_out12,
       decoder_1_out13, decoder_1_out14, decoder_1_out15, decoder_1_out16, decoder_1_out17, decoder_1_out18,
       decoder_1_out19, decoder_1_out20, decoder_1_out21, decoder_1_out22, decoder_1_out23, decoder_1_out24,
       decoder_1_out25, decoder_1_out26, decoder_1_out27, decoder_1_out28, decoder_1_out29, decoder_1_out30,
       decoder_1_out31;
  wire [31:0] MemCell_1_data_out, MemCell_2_data_out, MemCell_3_data_out, MemCell_4_data_out,
       MemCell_5_data_out, MemCell_6_data_out, MemCell_7_data_out, MemCell_8_data_out, MemCell_9_data_out,
       MemCell_10_data_out, MemCell_11_data_out, MemCell_12_data_out, MemCell_13_data_out,
       MemCell_14_data_out, MemCell_15_data_out, MemCell_16_data_out, MemCell_17_data_out,
       MemCell_18_data_out, MemCell_19_data_out, MemCell_20_data_out, MemCell_21_data_out,
       MemCell_22_data_out, MemCell_23_data_out, MemCell_24_data_out, MemCell_25_data_out,
       MemCell_26_data_out, MemCell_27_data_out, MemCell_28_data_out, MemCell_29_data_out,
       MemCell_30_data_out, MemCell_31_data_out, REG_0_1_data_out;

  Multiplexer #(.select(5), .width(32)) multiplexer_1 (
    .in0(REG_0_1_data_out), .in1(MemCell_1_data_out), .in2(MemCell_2_data_out), .in3(MemCell_3_data_out),
    .in4(MemCell_4_data_out), .in5(MemCell_5_data_out), .in6(MemCell_6_data_out), .in7(MemCell_7_data_out),
    .in8(MemCell_8_data_out), .in9(MemCell_9_data_out), .in10(MemCell_10_data_out),
    .in11(MemCell_11_data_out), .in12(MemCell_12_data_out), .in13(MemCell_13_data_out),
    .in14(MemCell_14_data_out), .in15(MemCell_15_data_out), .in16(MemCell_16_data_out),
    .in17(MemCell_17_data_out), .in18(MemCell_18_data_out), .in19(MemCell_19_data_out),
    .in20(MemCell_20_data_out), .in21(MemCell_21_data_out), .in22(MemCell_22_data_out),
    .in23(MemCell_23_data_out), .in24(MemCell_24_data_out), .in25(MemCell_25_data_out),
    .in26(MemCell_26_data_out), .in27(MemCell_27_data_out), .in28(MemCell_28_data_out),
    .in29(MemCell_29_data_out), .in30(MemCell_30_data_out), .in31(MemCell_31_data_out), .out(A_OUT),
    .sel(A_address));
  REG_0 REG_0_1 (.DATA_OUT(REG_0_1_data_out));
  MemCell MemCell_1 (.CL(CL), .write(decoder_1_out1), .DATA_IN(DATA_in), .DATA_OUT(MemCell_1_data_out));
  MemCell MemCell_2 (.CL(CL), .write(decoder_1_out2), .DATA_IN(DATA_in), .DATA_OUT(MemCell_2_data_out));
  MemCell MemCell_3 (.CL(CL), .write(decoder_1_out3), .DATA_IN(DATA_in), .DATA_OUT(MemCell_3_data_out));
  MemCell MemCell_4 (.CL(CL), .write(decoder_1_out4), .DATA_IN(DATA_in), .DATA_OUT(MemCell_4_data_out));
  MemCell MemCell_5 (.CL(CL), .write(decoder_1_out5), .DATA_IN(DATA_in), .DATA_OUT(MemCell_5_data_out));
  MemCell MemCell_6 (.CL(CL), .write(decoder_1_out6), .DATA_IN(DATA_in), .DATA_OUT(MemCell_6_data_out));
  MemCell MemCell_7 (.CL(CL), .write(decoder_1_out7), .DATA_IN(DATA_in), .DATA_OUT(MemCell_7_data_out));
  Decoder #(.select(5)) decoder_1 (
    .out1(decoder_1_out1), .out2(decoder_1_out2), .out3(decoder_1_out3), .out4(decoder_1_out4),
    .out5(decoder_1_out5), .out6(decoder_1_out6), .out7(decoder_1_out7), .out8(decoder_1_out8),
    .out9(decoder_1_out9), .out10(decoder_1_out10), .out11(decoder_1_out11), .out12(decoder_1_out12),
    .out13(decoder_1_out13), .out14(decoder_1_out14), .out15(decoder_1_out15), .out16(decoder_1_out16),
    .out17(decoder_1_out17), .out18(decoder_1_out18), .out19(decoder_1_out19), .out20(decoder_1_out20),
    .out21(decoder_1_out21), .out22(decoder_1_out22), .out23(decoder_1_out23), .out24(decoder_1_out24),
    .out25(decoder_1_out25), .out26(decoder_1_out26), .out27(decoder_1_out27), .out28(decoder_1_out28),
    .out29(decoder_1_out29), .out30(decoder_1_out30), .out31(decoder_1_out31), .sel(write_address), .en(write));  // open: out0
  MemCell MemCell_8 (.CL(CL), .write(decoder_1_out8), .DATA_IN(DATA_in), .DATA_OUT(MemCell_8_data_out));
  MemCell MemCell_9 (.CL(CL), .write(decoder_1_out9), .DATA_IN(DATA_in), .DATA_OUT(MemCell_9_data_out));
  MemCell MemCell_10 (.CL(CL), .write(decoder_1_out10), .DATA_IN(DATA_in), .DATA_OUT(MemCell_10_data_out));
  MemCell MemCell_11 (.CL(CL), .write(decoder_1_out11), .DATA_IN(DATA_in), .DATA_OUT(MemCell_11_data_out));
  MemCell MemCell_12 (.CL(CL), .write(decoder_1_out12), .DATA_IN(DATA_in), .DATA_OUT(MemCell_12_data_out));
  MemCell MemCell_13 (.CL(CL), .write(decoder_1_out13), .DATA_IN(DATA_in), .DATA_OUT(MemCell_13_data_out));
  MemCell MemCell_14 (.CL(CL), .write(decoder_1_out14), .DATA_IN(DATA_in), .DATA_OUT(MemCell_14_data_out));
  MemCell MemCell_15 (.CL(CL), .write(decoder_1_out15), .DATA_IN(DATA_in), .DATA_OUT(MemCell_15_data_out));
  MemCell MemCell_16 (.CL(CL), .write(decoder_1_out16), .DATA_IN(DATA_in), .DATA_OUT(MemCell_16_data_out));
  MemCell MemCell_17 (.CL(CL), .write(decoder_1_out17), .DATA_IN(DATA_in), .DATA_OUT(MemCell_17_data_out));
  MemCell MemCell_18 (.CL(CL), .write(decoder_1_out18), .DATA_IN(DATA_in), .DATA_OUT(MemCell_18_data_out));
  MemCell MemCell_19 (.CL(CL), .write(decoder_1_out19), .DATA_IN(DATA_in), .DATA_OUT(MemCell_19_data_out));
  MemCell MemCell_20 (.CL(CL), .write(decoder_1_out20), .DATA_IN(DATA_in), .DATA_OUT(MemCell_20_data_out));
  MemCell MemCell_21 (.CL(CL), .write(decoder_1_out21), .DATA_IN(DATA_in), .DATA_OUT(MemCell_21_data_out));
  MemCell MemCell_22 (.CL(CL), .write(decoder_1_out22), .DATA_IN(DATA_in), .DATA_OUT(MemCell_22_data_out));
  MemCell MemCell_23 (.CL(CL), .write(decoder_1_out23), .DATA_IN(DATA_in), .DATA_OUT(MemCell_23_data_out));
  MemCell MemCell_24 (.CL(CL), .write(decoder_1_out24), .DATA_IN(DATA_in), .DATA_OUT(MemCell_24_data_out));
  MemCell MemCell_25 (.CL(CL), .write(decoder_1_out25), .DATA_IN(DATA_in), .DATA_OUT(MemCell_25_data_out));
  MemCell MemCell_26 (.CL(CL), .write(decoder_1_out26), .DATA_IN(DATA_in), .DATA_OUT(MemCell_26_data_out));
  MemCell MemCell_27 (.CL(CL), .write(decoder_1_out27), .DATA_IN(DATA_in), .DATA_OUT(MemCell_27_data_out));
  MemCell MemCell_28 (.CL(CL), .write(decoder_1_out28), .DATA_IN(DATA_in), .DATA_OUT(MemCell_28_data_out));
  MemCell MemCell_29 (.CL(CL), .write(decoder_1_out29), .DATA_IN(DATA_in), .DATA_OUT(MemCell_29_data_out));
  MemCell MemCell_30 (.CL(CL), .write(decoder_1_out30), .DATA_IN(DATA_in), .DATA_OUT(MemCell_30_data_out));
  MemCell MemCell_31 (.CL(CL), .write(decoder_1_out31), .DATA_IN(DATA_in), .DATA_OUT(MemCell_31_data_out));
  Multiplexer #(.select(5), .width(32)) multiplexer_2 (
    .in0(REG_0_1_data_out), .in1(MemCell_1_data_out), .in2(MemCell_2_data_out), .in3(MemCell_3_data_out),
    .in4(MemCell_4_data_out), .in5(MemCell_5_data_out), .in6(MemCell_6_data_out), .in7(MemCell_7_data_out),
    .in8(MemCell_8_data_out), .in9(MemCell_9_data_out), .in10(MemCell_10_data_out),
    .in11(MemCell_11_data_out), .in12(MemCell_12_data_out), .in13(MemCell_13_data_out),
    .in14(MemCell_14_data_out), .in15(MemCell_15_data_out), .in16(MemCell_16_data_out),
    .in17(MemCell_17_data_out), .in18(MemCell_18_data_out), .in19(MemCell_19_data_out),
    .in20(MemCell_20_data_out), .in21(MemCell_21_data_out), .in22(MemCell_22_data_out),
    .in23(MemCell_23_data_out), .in24(MemCell_24_data_out), .in25(MemCell_25_data_out),
    .in26(MemCell_26_data_out), .in27(MemCell_27_data_out), .in28(MemCell_28_data_out),
    .in29(MemCell_29_data_out), .in30(MemCell_30_data_out), .in31(MemCell_31_data_out), .out(B_OUT),
    .sel(B_address));
endmodule

module MemCell (
  input  [31:0] DATA_IN,
  input  CL,
  input  write,
  output [31:0] DATA_OUT
);

  Register #(.width(32)) register_1 (.D(DATA_IN), .en(write), .clk(CL), .Q(DATA_OUT));  // open: clr
endmodule

module REG_0 (
  output [31:0] DATA_OUT
);


  assign DATA_OUT = {32{1'b0}};
endmodule

module IO (
  input  [2:0] deviceID,
  input  [31:0] DATA_OUT,
  input  OUTP,
  input  iNP,
  input  [31:0] i1,
  input  [31:0] i2,
  input  [31:0] i3,
  input  [31:0] i4,
  input  [31:0] i5,
  input  [31:0] i6,
  input  [31:0] i7,
  input  [31:0] i8,
  output [31:0] DATA_IN,
  output [31:0] o1,
  output [31:0] o2,
  output [31:0] o3,
  output [31:0] o4,
  output [31:0] o5,
  output [31:0] o6,
  output [31:0] o7,
  output [31:0] o8,
  output [1:0] io1,
  output [1:0] io2,
  output [1:0] io3,
  output [1:0] io4,
  output [1:0] io5,
  output [1:0] io6,
  output [1:0] io7,
  output [1:0] io8
);

  Multiplexer #(.select(3), .width(32)) multiplexer_1 (
    .in0(i1), .in1(i2), .in2(i3), .in3(i4), .in4(i5), .in5(i6), .in6(i7), .in7(i8), .out(DATA_IN),
    .sel(deviceID));
  Demultiplexer #(.select(3), .width(32)) demultiplexer_1 (
    .out0(o1), .out1(o2), .out2(o3), .out3(o4), .out4(o5), .out5(o6), .out6(o7), .out7(o8), .in(DATA_OUT),
    .sel(deviceID));
  Demultiplexer #(.select(3), .width(2)) demultiplexer_2 (
    .out0(io1), .out1(io2), .out2(io3), .out3(io4), .out4(io5), .out5(io6), .out6(io7), .out7(io8),
    .in({iNP, OUTP}), .sel(deviceID));
endmodule

module DisplayBuffer (
  input  CL,
  input  Inp,
  input  [31:0] DATA,
  output [23:0] RGB,
  output [6:0] X,
  output [6:0] Y,
  output Enable,
  output RESET,
  output clout
);

  wire counter_1_q, demultiplexer_1_out0, not_1_out;

  Counter #(.max('h1), .width(1)) counter_1 (
    .up(Inp), .count(Inp), .clk(CL), .Q(counter_1_q));  // open: clr, load, D, carry
  Demultiplexer demultiplexer_1 (.out0(demultiplexer_1_out0), .out1(Enable), .in(Inp), .sel(not_1_out));
  not not_1 (not_1_out, counter_1_q);
  Register #(.width(24)) register_1 (.D(DATA[23:0]), .en(demultiplexer_1_out0), .clk(CL), .Q(RGB));  // open: clr
  Pull_Resistor pull_resistor_1 (.node(DATA[31]));
  Pull_Resistor pull_resistor_2 (.node(Inp));
  and and_1 (RESET, Inp, DATA[31]);

  assign clout = CL;
  assign X = DATA[6:0];
  assign Y = DATA[13:7];
endmodule
